# Fritzing sketch heating system (saved by Fritzing 0.9.6b)
circuit board: 8.39643cm x 5.50396cm
breadboards: 1

parts:
  Heater = Heating Pad
  Mosfet = IFR520 MOS module [package=THT]
  YwRobot_Power_Supply1 = YwRobot Breadboard Power Supply [part_number=545043]
  Mod1 = Heltec WiFi LoRa 32 V2 [part_number=HTIT-WB32LA]
  M1 = RioRand LM2596  # not connected
  FAN = Fan - Ventilador [package=THT]
  1_Channel_Relay1 = 1 Channel Power Relay
  DS1 = DS18B20 1-Wire Temperature Sensor [part_number=DS18B20]
  DS2 = DS18B20 1-Wire Temperature Sensor [part_number=DS18B20]

nets:
  N1: Heater.pin_0, Mosfet.V+
  N2: Heater.pin_1, Mosfet.V-
  N3: Mosfet.SIG, Mod1.pin_36
  VCC: Mosfet.VCC, YwRobot_Power_Supply1.VCC5, Mod1.pin_16, Mod1.pin_17, Mod1.pin_20, Mod1.pin_21, Mod1.pin_22, 1_Channel_Relay1.VCC, DS1.VDD, DS2.VDD
  GND: Mosfet.GND, YwRobot_Power_Supply1.GND, Mod1.GND, FAN.GND, 1_Channel_Relay1.GND, DS1.GND, DS2.GND
  N4: YwRobot_Power_Supply1.VCC3, 1_Channel_Relay1.NO
  N5: Mod1.pin_2, 1_Channel_Relay1.IN, 1_Channel_Relay1.COM#11
  N6: Mod1.pin_28, DS1.DQ, DS2.DQ
  N7: FAN.5V, 1_Channel_Relay1.COM#14

notes:
  12V IN
  9V IN
  3V3 OUT
  5V OUT
  Ambient Temp Sensor
  9V OUT

custom parts:
  Heating Pad: A thermoresistant material with an embeded conductor that dissipates electrical energy into heat.
  YwRobot Breadboard Power Supply: The YwRobot Breadboard Power Supply (MB-V2) has two power rails; they can be 5V or 3V3. Power to the module can be provided through the female USB socket or through the A10 (female) 2.1mm power jack.
  Fan - Ventilador: Ventilador de 2 pines, se encuentra comunmente en computadoras de escritorio
  1 Channel Power Relay: A 1 channel power relay. The module operates at 5V.
