# Fritzing sketch heating system (saved by Fritzing 0.9.6b)
circuit board: 8.39643cm x 5.50396cm
breadboards: 1
stripboards: 1

parts:
  Heater = Heating Pad
  Mosfet = IFR520 MOS module [package=THT]
  YwRobot_Power_Supply1 = YwRobot Breadboard Power Supply [part_number=545043]
  Mod1 = Heltec WiFi LoRa 32 V2 [part_number=HTIT-WB32LA]
  Jack_12V = Power Jack [package=power_jack_pth_lock]
  M1 = RioRand LM2596
  J1 = Power Jack [package=power_jack_slot]
  FAN = Fan - Ventilador [package=THT]
  1_Channel_Relay1 = 1 Channel Power Relay

nets (from the breadboard view):
  N1: Heater.pin_0, Mosfet.V+
  N2: Heater.pin_1, Mosfet.V-
  N3: Mosfet.SIG, Mod1.pin_36
  VCC: Mosfet.VCC, YwRobot_Power_Supply1.VCC5, Mod1.pin_20, 1_Channel_Relay1.VCC
  GND: Mosfet.GND, YwRobot_Power_Supply1.GND, Mod1.GND, Jack_12V.GND, FAN.GND, 1_Channel_Relay1.GND
  N4: Mosfet.VIN, Jack_12V.PWR
  N5: YwRobot_Power_Supply1.VCC3, Mod1.pin_16, Mod1.pin_17, 1_Channel_Relay1.NO
  N6: Mod1.pin_2, 1_Channel_Relay1.IN, 1_Channel_Relay1.COM#11
  N7: Mod1.pin_21, Mod1.pin_22
  N8: M1.Pin_1, J1.PWR
  N9: M1.Pin_2, J1.GNDBREAK, J1.GND
  N10: FAN.5V, 1_Channel_Relay1.COM#14

notes:
  12V
  9V
  3V3
  5V

custom parts:
  Heating Pad: A thermoresistant material with an embeded conductor that dissipates electrical energy into heat.
  YwRobot Breadboard Power Supply: The YwRobot Breadboard Power Supply (MB-V2) has two power rails; they can be 5V or 3V3. Power to the module can be provided through the female USB socket or through the A10 (female) 2.1mm power jack.
  Fan - Ventilador: Ventilador de 2 pines, se encuentra comunmente en computadoras de escritorio
  1 Channel Power Relay: A 1 channel power relay. The module operates at 5V.
